// Logisim project Cache.circ as structural Verilog: 10 circuits, main circuit main
module main (
  input  [15:0] in_1,
  input  in_2,
  input  in_3
);

  wire CacheToReg, clock, IsBranch, Jump, multiplexer_7_out, not_1_out, not_2_out, not_3_out, stall, stall2,
       store;
  wire [9:0] adder_1_out, address, addressPC, Desloc, JumpAddress, multiplexer_1_out, multiplexer_2_out,
       multiplexer_3_out, multiplexer_4_out, ReadAddress;
  wire [15:0] data, data1, data2, data3, data4, multiplexer_5_out, outputcache, outputmp, register_1_q;

  Clock clock_1 (.out(clock));
  Multiplexer #(.width(10), .enable("false")) multiplexer_1 (
    .in0(multiplexer_4_out), .in1(10'h4), .out(multiplexer_1_out), .sel(in_3));
  not not_1 (not_1_out, stall);
  Multiplexer #(.width(10), .enable("false")) multiplexer_2 (
    .in0(10'h1), .in1({10{1'b0}}), .out(multiplexer_2_out), .sel(stall2));
  Register #(.width(10)) PC (.D(multiplexer_1_out), .en(1'b1), .Q(addressPC), .clk(clock));  // open: clr
  MP Memoria_Principal (
    .inputData(in_1), .store(in_2), .address(address), .outputData(data1), .outputData_2(data2),
    .outputData_3(data3), .outputData_4(data4));
  J_K_Flip_Flop j_k_ff_1 (.J(stall), .clk(clock), .K(not_1_out), .Q(store));  // open: Qn, preset, en, reset
  Adder #(.width(10)) adder_1 (.a(multiplexer_2_out), .b(addressPC), .out(adder_1_out));  // open: cin, cout
  or or_1 (stall2, stall, store);
  Multiplexer #(.width(10), .enable("false")) multiplexer_3 (
    .in0(adder_1_out), .in1(Desloc), .out(multiplexer_3_out), .sel(IsBranch));
  not not_2 (not_2_out, Jump);
  Controle_cache ControleCache (.row(address[4:2]), .cacheStatus(stall), .Tag(address[9:5]), .store(store));
  Multiplexer #(.width(10), .enable("false")) multiplexer_4 (
    .in0(JumpAddress), .in1(multiplexer_3_out), .out(multiplexer_4_out), .sel(not_2_out));
  Cache Memoria_Cache (
    .input1(data1), .input2(data2), .input3(data3), .input4(data4), .row(address[4:2]), .word(address[1:0]),
    .store(store), .out_8(outputcache));
  // NOT_Gate not_3 has open pins: in=open, out=not_3_out
  Multiplexer #(.width(16), .enable("false")) multiplexer_5 (
    .in0(data), .in1({16{1'b0}}), .out(multiplexer_5_out), .sel(stall2));
  Register #(.width(16)) register_1 (.D(data), .en(not_3_out), .Q(register_1_q), .clk(clock));  // open: clr
  Multiplexer #(.width(10), .enable("false")) multiplexer_6 (
    .in0(addressPC), .in1(ReadAddress), .out(address), .sel(multiplexer_7_out));
  Multiplexer #(.enable("false")) multiplexer_7 (.in0(1'b0), .in1(CacheToReg), .out(multiplexer_7_out));  // open: sel
  Processador processador_1 (
    .dado(multiplexer_5_out), .Instrucao(register_1_q), .Deslocamento(Desloc), .IsBranch(IsBranch),
    .Jump(Jump), .JumpAddress(JumpAddress), .readAddress(ReadAddress), .out_8(CacheToReg));
  Multiplexer #(.select(2), .width(16), .enable("false")) multiplexer_8 (
    .in0(data1), .in1(data2), .in2(data3), .in3(data4), .out(outputmp), .sel(address[1:0]));
  Multiplexer #(.width(16), .enable("false")) multiplexer_9 (
    .in0(outputcache), .in1(outputmp), .out(data), .sel(store));

  // Other names for the same wires on the sheet: tag[4:0] = address[9:5]; reset = in_3; row[2:0] = address[4:2];
  //   word[1:0] = address[1:0]

  // Notes on the sheet:
  //   PC
endmodule

module MP (
  input  [15:0] inputData,
  input  store,
  input  [9:0] address,
  output [15:0] outputData,
  output [15:0] outputData_2,
  output [15:0] outputData_3,
  output [15:0] outputData_4
);

  wire CLK, demultiplexer_1_out0, demultiplexer_1_out1, demultiplexer_1_out2, demultiplexer_1_out3,
       not_1_out, not_2_out, not_3_out, not_4_out;

  Clock clock_1 (.out(CLK));
  Demultiplexer #(.select(2), .enable("false")) demultiplexer_1 (
    .out0(demultiplexer_1_out0), .out1(demultiplexer_1_out1), .out2(demultiplexer_1_out2),
    .out3(demultiplexer_1_out3), .in(store), .sel(address[1:0]));
  assign outputData = demultiplexer_1_out0 ? inputData : 16'bz;  // Controlled_Buffer controlled_buffer_1
  assign outputData_2 = demultiplexer_1_out1 ? inputData : 16'bz;  // Controlled_Buffer controlled_buffer_2
  assign outputData_3 = demultiplexer_1_out2 ? inputData : 16'bz;  // Controlled_Buffer controlled_buffer_3
  assign outputData_4 = demultiplexer_1_out3 ? inputData : 16'bz;  // Controlled_Buffer controlled_buffer_4
  not not_1 (not_1_out, demultiplexer_1_out0);
  not not_2 (not_2_out, demultiplexer_1_out1);
  not not_3 (not_3_out, demultiplexer_1_out2);
  not not_4 (not_4_out, demultiplexer_1_out3);
  RAM #(.dataWidth(16)) ram_1 (.addr(address[9:2]), .data(outputData), .clk(CLK), .ld(not_1_out));  // open: sel, clr
  RAM #(.dataWidth(16)) ram_2 (.addr(address[9:2]), .data(outputData_2), .clk(CLK), .ld(not_2_out));  // open: sel, clr
  RAM #(.dataWidth(16)) ram_3 (.addr(address[9:2]), .data(outputData_3), .clk(CLK), .ld(not_3_out));  // open: sel, clr
  RAM #(.dataWidth(16)) ram_4 (.addr(address[9:2]), .data(outputData_4), .clk(CLK), .ld(not_4_out));  // open: sel, clr
endmodule

module Linha (
  input  [15:0] inputData1,
  input  [15:0] inputData2,
  input  store,
  input  [15:0] inputData3,
  input  [1:0] word,
  input  [15:0] inputData4,
  output [15:0] \output 
);

  wire CLK;
  wire [15:0] output1, output2, output3, output4;

  Clock clock_1 (.out(CLK));
  Register #(.width(16)) register_1 (.D(inputData1), .en(store), .Q(output1), .clk(CLK));  // open: clr
  Register #(.width(16)) register_2 (.D(inputData2), .en(store), .Q(output2), .clk(CLK));  // open: clr
  Register #(.width(16)) register_3 (.D(inputData3), .en(store), .Q(output3), .clk(CLK));  // open: clr
  Register #(.width(16)) register_4 (.D(inputData4), .en(store), .Q(output4), .clk(CLK));  // open: clr
  Multiplexer #(.select(2), .width(16), .enable("false")) multiplexer_1 (
    .in0(output1), .in1(output2), .in2(output3), .in3(output4), .out(\output ), .sel(word));
endmodule

module Cache (
  input  [15:0] input1,
  input  [15:0] input2,
  input  [15:0] input3,
  input  [15:0] input4,
  input  [2:0] row,
  input  [1:0] word,
  input  store,
  output [15:0] out_8
);

  wire row1, row2, row3, row4, row5, row6, row7, row8;
  wire [15:0] output1, output2, output3, output4, output5, output6, output7, output8;

  Demultiplexer #(.select(3), .enable("false")) demultiplexer_1 (
    .out0(row1), .out1(row2), .out2(row3), .out3(row4), .out4(row5), .out5(row6), .out6(row7), .out7(row8),
    .in(store), .sel(row));
  Linha linha_1 (
    .inputData1(input1), .inputData2(input2), .inputData3(input3), .store(row1), .word(word),
    .inputData4(input4), .\output (output1));
  Linha linha_2 (
    .inputData1(input1), .inputData2(input2), .inputData3(input3), .store(row2), .word(word),
    .inputData4(input4), .\output (output2));
  Linha linha_3 (
    .inputData1(input1), .inputData2(input2), .inputData3(input3), .store(row3), .word(word),
    .inputData4(input4), .\output (output3));
  Linha linha_4 (
    .inputData1(input1), .inputData2(input2), .inputData3(input3), .store(row4), .word(word),
    .inputData4(input4), .\output (output4));
  Linha linha_5 (
    .inputData1(input1), .inputData2(input2), .inputData3(input3), .store(row5), .word(word),
    .inputData4(input4), .\output (output5));
  Linha linha_6 (
    .inputData1(input1), .inputData2(input2), .inputData3(input3), .store(row6), .word(word),
    .inputData4(input4), .\output (output6));
  Linha linha_7 (
    .inputData1(input1), .inputData2(input2), .inputData3(input3), .store(row7), .word(word),
    .inputData4(input4), .\output (output7));
  Linha linha_8 (
    .inputData1(input1), .inputData2(input2), .inputData3(input3), .store(row8), .word(word),
    .inputData4(input4), .\output (output8));
  Multiplexer #(.select(3), .width(16), .enable("false")) multiplexer_1 (
    .in0(output1), .in1(output2), .in2(output3), .in3(output4), .in4(output5), .in5(output6), .in6(output7),
    .in7(output8), .out(out_8), .sel(row));

  // Other names for the same wires on the sheet: word1[15:0] = input1; word2[15:0] = input2; word3[15:0] = input3;
  //   word4[15:0] = input4
endmodule

// CC
module Controle_cache (
  input  [4:0] Tag,
  input  store,
  input  [2:0] row,
  output cacheStatus
);

  wire CLK, comparator_1_eq, not_1_out;
  wire [5:0] bit_extender_1_out, controlled_buffer_1_out, Tag_t;

  Clock clock_1 (.out(CLK));
  Adder #(.width(6)) adder_1 (.a(6'b000001), .b(bit_extender_1_out), .out(Tag_t));  // open: cin, cout
  assign bit_extender_1_out = {{1{1'b0}}, Tag};  // Bit_Extender bit_extender_1
  assign controlled_buffer_1_out = store ? Tag_t : 6'bz;  // Controlled_Buffer controlled_buffer_1
  not not_1 (not_1_out, store);
  RAM #(.addrWidth(3), .dataWidth(6)) ram_1 (
    .addr(row), .data(controlled_buffer_1_out), .clk(CLK), .ld(not_1_out));  // open: sel, clr
  Comparator #(.width(6)) comparator_1 (.a(controlled_buffer_1_out), .b(Tag_t), .eq(comparator_1_eq));  // open: gt, lt
  not not_2 (cacheStatus, comparator_1_eq);

  // Notes on the sheet:
  //   Soma 1 a tag para ignorar a Tag 0
  //   Armazena a Tag
  //   CacheStatus:
  //   0 - Cache Hit
  //   1 - Cache Miss
endmodule

module Processador (
  input  [15:0] dado,
  input  [15:0] Instrucao,
  output [9:0] Deslocamento,
  output IsBranch,
  output Jump,
  output [9:0] JumpAddress,
  output [9:0] readAddress,
  output out_8
);

  wire AluSrc, Branch, CacheRead, CacheWrite, Clock, RegDst, RegWrite, ula_1_igual;
  wire [1:0] controleula_1_controle;
  wire [2:0] ALUOP;
  wire [15:0] \banco_de_registradores_1_saída1 , \banco_de_registradores_1_saída2 , bit_extender_2_out,
       Dado_t, multiplexer_1_out;
  wire [15:10] \ula_1_saída ;

  Clock u_clock (.out(Clock));
  assign Deslocamento = {{3{1'b0}}, {Instrucao[0], Instrucao[1], Instrucao[2], Instrucao[3], Instrucao[4], Instrucao[5], Instrucao[6]}};  // Bit_Extender bit_extender_1
  Unidade_de_Controle unidade_de_controle_1 (
    .RegDst(RegDst), .RegWrite(RegWrite), .ALUSrc(AluSrc), .MemRead(CacheRead), .MemWrite(CacheWrite),
    .Branch(Branch), .MemToReg(out_8), .Jump(Jump), .opcode(Instrucao[15:13]), .ALUOP(ALUOP));
  Banco_de_Registradores banco_de_registradores_1 (
    .WriteAddress(Instrucao[12:10]), .ReadAddress1(Instrucao[9:7]), .ReadAddress2(Instrucao[6:4]),
    .RegWrite(RegWrite), .Dados(Dado_t), .\Saída1 (\banco_de_registradores_1_saída1 ),
    .\Saída2 (\banco_de_registradores_1_saída2 ));
  assign bit_extender_2_out = {{6{1'b0}}, Deslocamento};  // Bit_Extender bit_extender_2
  Multiplexer #(.width(16), .enable("false")) multiplexer_1 (
    .in0(\banco_de_registradores_1_saída2 ), .in1(bit_extender_2_out), .out(multiplexer_1_out), .sel(AluSrc));
  ULA ula_1 (
    .Entrada1(\banco_de_registradores_1_saída1 ), .Entrada2(multiplexer_1_out),
    .Function(controleula_1_controle), .\Saída ({\ula_1_saída , readAddress}), .Igual(ula_1_igual));
  ControleULA controleula_1 (.Function(Instrucao[1:0]), .Controle(controleula_1_controle), .ALUOP(ALUOP));
  and and_1 (IsBranch, Branch, ula_1_igual);
  Multiplexer #(.width(16), .enable("false")) multiplexer_2 (
    .in0({\ula_1_saída , readAddress}), .in1(dado), .out(Dado_t), .sel(out_8));

  assign JumpAddress = Instrucao[12:3];

  // Other names for the same wires on the sheet: JumpIMM[9:0] = Instrucao[12:3]; CacheToReg = out_8;
  //   DadoCache[15:0] = dado; Desloc[9:0] = Deslocamento; function[1:0] = Instrucao[1:0];
  //   opcode[2:0] = Instrucao[15:13]; RD[2:0] = Instrucao[12:10]; RS[2:0] = Instrucao[9:7]; RT[2:0] = Instrucao[6:4]
endmodule

module ULA (
  input  [15:0] Entrada1,
  input  [15:0] Entrada2,
  input  [1:0] Function,
  output [15:0] \Saída ,
  output Igual
);

  wire [15:0] AND, OR, Soma, \Subtração ;

  Adder #(.width(16)) adder_1 (.a(Entrada1), .b(Entrada2), .out(Soma));  // open: cin, cout
  Subtractor #(.width(16)) subtractor_1 (.a(Entrada1), .b(Entrada2), .out(\Subtração ));  // open: bin, bout
  assign AND = Entrada1 & Entrada2;  // AND_Gate and_1, 16 bits wide
  assign OR = Entrada1 | Entrada2;  // OR_Gate or_1, 16 bits wide
  Multiplexer #(.select(2), .width(16), .enable("false")) multiplexer_1 (
    .in0(Soma), .in1(\Subtração ), .in2(AND), .in3(OR), .out(\Saída ), .sel(Function));
  nor nor_1 (Igual, \Subtração [0], \Subtração [1], \Subtração [2], \Subtração [3], \Subtração [4], \Subtração [5], \Subtração [6], \Subtração [7], \Subtração [8], \Subtração [9], \Subtração [10], \Subtração [11], \Subtração [12], \Subtração [13], \Subtração [14], \Subtração [15]);
endmodule

module Banco_de_Registradores (
  input  [2:0] WriteAddress,
  input  [2:0] ReadAddress1,
  input  [2:0] ReadAddress2,
  input  RegWrite,
  input  [15:0] Dados,
  output [15:0] \Saída1 ,
  output [15:0] \Saída2 
);

  wire clock_1_out, write_r1, write_r2, write_r3, write_r4, write_r5, write_r6, write_r7;
  wire [15:0] r0, r1, r2, r3, r4, r5, r6, r7;

  Demultiplexer #(.select(3), .enable("false")) demultiplexer_1 (
    .out1(write_r1), .out2(write_r2), .out3(write_r3), .out4(write_r4), .out5(write_r5), .out6(write_r6),
    .out7(write_r7), .in(RegWrite), .sel(WriteAddress));  // open: out0
  Register #(.width(16)) register_1 (.D({16{1'b0}}), .Q(r0), .clk(clock_1_out));  // open: en, clr
  Register #(.width(16)) register_2 (.D(Dados), .en(write_r1), .Q(r1), .clk(clock_1_out));  // open: clr
  Register #(.width(16)) register_3 (.D(Dados), .en(write_r2), .Q(r2), .clk(clock_1_out));  // open: clr
  Register #(.width(16)) register_4 (.D(Dados), .en(write_r3), .Q(r3), .clk(clock_1_out));  // open: clr
  Register #(.width(16)) register_5 (.D(Dados), .en(write_r4), .Q(r4), .clk(clock_1_out));  // open: clr
  Register #(.width(16)) register_6 (.D(Dados), .en(write_r5), .Q(r5), .clk(clock_1_out));  // open: clr
  Register #(.width(16)) register_7 (.D(Dados), .en(write_r6), .Q(r6), .clk(clock_1_out));  // open: clr
  Register #(.width(16)) register_8 (.D(Dados), .en(write_r7), .Q(r7), .clk(clock_1_out));  // open: clr
  Clock clock_1 (.out(clock_1_out));
  Multiplexer #(.select(3), .width(16), .enable("false")) multiplexer_1 (
    .in0(r0), .in1(r1), .in2(r2), .in3(r3), .in4(r4), .in5(r5), .in6(r6), .in7(r7), .out(\Saída1 ),
    .sel(ReadAddress1));
  Multiplexer #(.select(3), .width(16), .enable("false")) multiplexer_2 (
    .in0(r0), .in1(r1), .in2(r2), .in3(r3), .in4(r4), .in5(r5), .in6(r6), .in7(r7), .out(\Saída2 ),
    .sel(ReadAddress2));

  // Other names for the same wires on the sheet: Dado[15:0] = Dados; saida1[15:0] = \Saída1 ; saida2[15:0] = \Saída2 
endmodule

// Unidade Controle
module Unidade_de_Controle (
  input  [2:0] opcode,
  output RegDst,
  output RegWrite,
  output ALUSrc,
  output MemRead,
  output MemWrite,
  output Branch,
  output MemToReg,
  output Jump,
  output [2:0] ALUOP
);

  Multiplexer #(.select(3), .width(11), .enable("false")) multiplexer_1 (
    .in0(11'h203), .in1(11'h4f), .in2(11'h14), .in3(11'h7), .in4(11'h307), .in5(11'h407), .in6(11'h20),
    .in7(11'h80), .out({ALUOP, Jump, MemToReg, Branch, MemWrite, MemRead, ALUSrc, RegWrite, RegDst}),
    .sel(opcode));
endmodule

module ControleULA (
  input  [1:0] Function,
  input  [2:0] ALUOP,
  output [1:0] Controle
);

  Multiplexer #(.select(3), .width(2), .enable("false")) multiplexer_1 (
    .in0(2'b00), .in1(2'b01), .in2(Function), .in3(2'b10), .in4(2'b11), .out(Controle), .sel(ALUOP));  // open: in5, in6, in7

  // Notes on the sheet:
  //   ADD
  //   SUB
  //   AND
  //   OR
endmodule
